# Fritzing sketch Hardware_Equipo13 (saved by Fritzing 0.9.3b)
breadboards: 1

parts:
  VCC1 = Battery block 9V
  R6 = Resistor [tolerance=±5% resistance=100 package="0805 [SMD]"]
  Convertidor_de_Voltaje1 = Breadboard Power Supply Board SMD
  Switch1 = Toggle Switch [package=THT]
  Arduino_Nano1 = Arduino Nano (Rev3.0) (ICSP)
  PD5 = S1133 Si Photodiode [package="8mm Ceramic [THT]"]
  PD6 = S1133 Si Photodiode [package="8mm Ceramic [THT]"]
  PD7 = S1133 Si Photodiode [package="8mm Ceramic [THT]"]
  Buzzer1 = Piezo Speaker
  LED5 = LED - 5mm [color="Green (570nm)" package="5 mm [THT]"]
  LED8 = LED - 5mm [color="Blue (470nm)" package="5 mm [THT]"]
  R9 = Resistor [tolerance=±5% resistance=1k package="0805 [SMD]"]
  R10 = Resistor [tolerance=±5% resistance=1k package="0805 [SMD]"]
  R11 = Resistor [tolerance=±5% resistance=1k package="0805 [SMD]"]
  R12 = Resistor [tolerance=±5% resistance=1k package="0805 [SMD]"]
  R13 = Resistor [tolerance=±5% resistance=1k package="0805 [SMD]"]
  LED9 = LED - 5mm [color="Blue (470nm)" package="5 mm [THT]"]
  LED10 = LED - 5mm [color="Green (570nm)" package="5 mm [THT]"]
  R15 = Resistor [tolerance=±5% resistance=100 package="0805 [SMD]"]
  J2 = Display LCD 2.2 inch ILI9341 [form="♀ (female)" package=THT]
  R16 = Resistor [tolerance=±5% resistance=1k package="0805 [SMD]"]
  PD8 = S1133 Si Photodiode [package="8mm Ceramic [THT]"]

nets:
  GND: VCC1.-, Convertidor_de_Voltaje1.GND, Switch1.L1, Arduino_Nano1.GND, PD5.cathode, PD6.cathode, PD7.cathode, Buzzer1.pin1, LED5.cathode, LED8.cathode, LED9.cathode, LED10.cathode, J2.GND, PD8.cathode
  N1: VCC1.+, Convertidor_de_Voltaje1.VIN
  N2: R6.Pin_0, Arduino_Nano1.D7
  N3: R6.Pin_1, LED5.anode, LED10.anode
  N4: Convertidor_de_Voltaje1.VCC, Switch1.L2
  5V: Switch1.COM, Arduino_Nano1.5V, J2.VCC, J2.LED
  N5: Arduino_Nano1.D0/RX, PD8.anode
  N6: Arduino_Nano1.D2, PD7.anode
  N7: Arduino_Nano1.D3, PD6.anode
  N8: Arduino_Nano1.D4, PD5.anode
  N9: Arduino_Nano1.D5, Buzzer1.pin2
  N10: Arduino_Nano1.D6, R15.Pin_0
  N11: Arduino_Nano1.D8, R9.Pin_0
  N12: Arduino_Nano1.D9, R10.Pin_0
  N13: Arduino_Nano1.D10, R11.Pin_0
  N14: Arduino_Nano1.D11/MOSI, R13.Pin_0
  N15: Arduino_Nano1.D12/MISO, R16.Pin_0
  N16: Arduino_Nano1.D13/SCK, R12.Pin_0
  N17: LED8.anode, LED9.anode, R15.Pin_1
  N18: R9.Pin_1, J2.DC/RS
  N19: R10.Pin_1, J2.RST
  N20: R11.Pin_1, J2.CS
  N21: R12.Pin_1, J2.SCK
  N22: R13.Pin_1, J2.MOSI
  N23: J2.MISO, R16.Pin_1

custom parts:
  Display LCD 2.2 inch ILI9341: Generic female header
